# Fritzing sketch Input_Circuit (saved by Fritzing 0.9.2b)
breadboards: 1

parts:
  R1 = Resistor [tolerance=±5% resistance=100k package=THT]
  R2 = Rotary Potentiometer (Small) [maximum_resistance=50kΩ package=THT]
  R3 = Resistor [tolerance=±5% resistance=100k package=THT]

nets:
  N1: R1.Pin_0, R3.Pin_1
  N2: R1.Pin_1, R2.leg1

notes:
  Ground
  5 V PSU
  + Basys 3 Pins
  -
